# Fritzing sketch Block Schematic (saved by Fritzing 0.9.0b)
breadboards: 1

parts:
  Part1 = Arduino Uno (Rev3)
  Part2 = SRF05 Ultrasonic Rangefinder
  Part3 = Logic Level Converter Bi-Directional BOB-12009
  DRV1 = DRV8824  # not connected
  Part4 = Bluetooth Mate Silver
  M1 = DC Motor  # not connected
  M2 = DC Motor  # not connected
  VCC1 = Battery block 9V

nets:
  GND: Part1.GND, Part2.GND, Part3.GND, Part4.RTS_5V, VCC1.-
  N1: Part1.D0/RX, Part4.RX_5V
  N2: Part1.D1/TX, Part4.TX_5V
  N3: Part1.D4, Part2.Echo
  N4: Part1.D7, Part2.Trig
  5V: Part1.5V, Part2.VCC, Part3.LV, Part3.HV
  N5: Part3.LV4, Part3.HV4
  N6: Part3.LV3, Part3.HV3
  N7: Part3.LV2, Part3.HV2
  N8: Part3.LV1, Part3.HV1

custom parts:
  Logic Level Converter Bi-Directional BOB-12009: SparkFun product BOB-12009 If you’ve ever tried to connect a 3.3V device to a 5V system, you know what a challenge it can be. The SparkFun bi-directional logic level converter is a small device that safely steps down 5V signals to 3.3V AND steps up 3.3V to 5V at the same time. This level converter also works with 2.8V and 1.8V devices. What really separates this Logic level converter from our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
  DRV8824: Pololu DRV8824 Stepper Motor Control Breakout The DRV8824 stepper motor driver carrier is a breakout board for TI’s DRV8824 microstepping bipolar stepper motor driver, a lower-current version of the DRV8825. The DRV8824 carrier can only deliver up to 0.75 A per coil without a heat sink (it is rated for up to 1.2 A per coil with sufficient additional cooling), but it has larger current-sense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
