# Fritzing sketch Circuit Schematic (saved by Fritzing 0.9.0b)
breadboards: 1

parts:
  Part1 = Arduino Uno (Rev3)
  Part2 = SRF05 Ultrasonic Rangefinder
  DRV1 = DRV8824
  M1 = DC Motor
  M2 = DC Motor
  Part4 = Logic Level Converter Bi-Directional BOB-12009
  Part6 = Bluetooth Mate Silver

nets:
  N1: Part1.D10_PWM/SS, DRV1.14_-_GND_motor
  N2: Part1.D11_PWM/MOSI, DRV1.15_-_VMOT
  GND: Part1.GND, Part2.GND, DRV1.12_-_B1, Part4.GND, Part6.GND
  N3: Part1.D0/RX, Part6.RX_5V
  N4: Part1.D1/TX, Part6.TX_5V
  N5: Part1.D4, Part2.Echo
  N6: Part1.D5_PWM, DRV1.8_-_GND_logic
  N7: Part1.D6_PWM, DRV1.9_-_/FAULT
  N8: Part1.D7, Part2.Trig
  5V: Part1.5V, Part2.VCC, Part4.HV
  N9: Part1.VIN, DRV1.13_-_B2
  N10: DRV1.1_-_M0, M1.pin_1
  N11: DRV1.3_-_M2, M1.pin_2
  N12: DRV1.4_-_RESET, M2.pin_1
  N13: DRV1.6_-_STEP, M2.pin_2
  N14: Part4.LV, Part6.VCC

custom parts:
  DRV8824: Pololu DRV8824 Stepper Motor Control Breakout The DRV8824 stepper motor driver carrier is a breakout board for TI’s DRV8824 microstepping bipolar stepper motor driver, a lower-current version of the DRV8825. The DRV8824 carrier can only deliver up to 0.75 A per coil without a heat sink (it is rated for up to 1.2 A per coil with sufficient additional cooling), but it has larger current-sense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
  Logic Level Converter Bi-Directional BOB-12009: SparkFun product BOB-12009 If you’ve ever tried to connect a 3.3V device to a 5V system, you know what a challenge it can be. The SparkFun bi-directional logic level converter is a small device that safely steps down 5V signals to 3.3V AND steps up 3.3V to 5V at the same time. This level converter also works with 2.8V and 1.8V devices. What really separates this Logic level converter from our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
